# Fritzing sketch Shield_LCD_Arduino (saved by Fritzing 0.8.5b)
circuit board: 8.46667cm x 5.64444cm

parts:
  Componente1 = Arduino Uno (Rev3)
  R1 = Trimmer Potentiometer [maximum_resistance=10kΩ package=THT]
  LCD1 = LCD screen
  R2 = Resistor [tolerance=±20% resistance=220k package=THT]

nets:
  GND: Componente1.GND, R1.leg1, LCD1.VSS, LCD1.R/W, LCD1.LED-
  N1: Componente1.D2, LCD1.RS
  N2: Componente1.D3_PWM, LCD1.E
  N3: Componente1.D4, LCD1.DB4
  N4: Componente1.D5_PWM, LCD1.DB5
  N5: Componente1.D6_PWM, LCD1.DB6
  N6: Componente1.D7, LCD1.DB7
  5V: Componente1.5V, R1.leg2, LCD1.VDD, R2.Pin_0
  N7: R1.wiper, LCD1.V0
  N8: LCD1.LED+, R2.Pin_1
